# Fritzing sketch 328_term (saved by Fritzing 0.9.1b)
breadboards: 1

parts:
  JP1 = RCA [package=rca_lock]
  U1 = mini DIN 6 Connector [package=mini-din6]
  U2 = atmega328 [package=dip]
  U3 = atmega328 [package=dip]
  D1_1N4148 = Diode [package=diode-1n4148]
  D2_1N4148 = Diode [package=diode-1n4148]
  R1 = Resistor [tolerance=±5% resistance=1k package="1206 [SMD]"]
  R2 = Resistor [tolerance=±5% resistance=330 package="1206 [SMD]"]
  XTAL1 = Crystal [frequency="16 Mhz" package=THT]
  C1_-_22pf = Capacitor [package=cap-pth-small2]
  C2_-_22pf = Capacitor [package=cap-pth-small2]
  XTAL2 = Crystal [frequency="16 Mhz" package=THT]
  C3_-_22pf1 = Capacitor [package=cap-pth-small2]
  C4_-_22pf1 = Capacitor [package=cap-pth-small2]
  IC1 = Voltage Regulator [package=to220-igo]
  C1 = Ceramic Capacitor [capacitance=100nF package="100 mil [THT, multilayer]"]
  C2 = Ceramic Capacitor [capacitance=100nF package="100 mil [THT, multilayer]"]
  C3 = Ceramic Capacitor [capacitance=100nF package="100 mil [THT, multilayer]"]
  C4 = Ceramic Capacitor [capacitance=100nF package="100 mil [THT, multilayer]"]
  C5 = Capacitor Polarized [package=cpol-radial-10uf-25v]  # not connected
  C6 = Capacitor Polarized [package=cpol-radial-10uf-25v]
  R3 = Resistor [tolerance=±5% resistance=10k package=THT]
  R4 = Resistor [tolerance=±5% resistance=10k package=THT]
  LED1 = LED - 5mm [color="Red (633nm)" package="5 mm [THT]"]

nets:
  N1: JP1.PIN, R1.Pin_1, R2.Pin_1
  GND: JP1.SHELL, U1.6, U2.GND, U3.GND#21, C1_-_22pf.2, C2_-_22pf.2, C3_-_22pf1.2, C4_-_22pf1.2, IC1.GND, C1.1, C3.0, C4.1, C6.-, LED1.cathode
  5V: U1.3, U2.AVCC, U3.VCC, U3.AVCC, IC1.IN, C1.0, C2.1, C4.0, C6.+, R3.Pin_1, R4.Pin_1
  N2: U1.4, U2.D3_(PWM)
  N3: U1.5, U2.D2
  N4: U2.RESET, R3.Pin_0
  N5: U2.D0_(RX), U3.D1_(TX)
  N6: U2.D1_(TX), U3.D0_(RX)
  N7: U2.VCC, C3.1
  N8: U2.XLAT1, XTAL2.pin_1, C3_-_22pf1.1
  N9: U2.XLAT2, XTAL2.pin_0, C4_-_22pf1.1
  N10: U3.RESET, R4.Pin_0
  N11: U3.GND#7, C2.0
  N12: U3.XLAT1, XTAL1.pin_1, C2_-_22pf.1
  N13: U3.XLAT2, XTAL1.pin_0, C1_-_22pf.1
  N14: U3.D9_(PWM), D1_1N4148.A
  N15: U3.D11_(PWM), D2_1N4148.A
  N16: D1_1N4148.C, R1.Pin_0
  N17: D2_1N4148.C, R2.Pin_0
  N18: IC1.OUT, LED1.anode

notes:
  sig_pixel
  sig_sync
  data
  clk
